# Fritzing sketch Door-Lock (saved by Fritzing 0.9.3b)

parts:
  Parça1 = Arduino Nano (Rev3.0)
  S1 = Toggle Switch [package=THT]
  LED1 = LED - 5mm [color="Red (633nm)" package="5 mm [THT]"]
  VCC2 = 4 x AAA Battery Mount
  J1 = Basic Servo
  Mod1 = KY-005 Infrared Transmitter Module [package="Breakout board"]

nets:
  GND: Parça1.GND, VCC2.-, J1.gnd
  N1: Parça1.D2, Mod1.S
  N2: Parça1.D3, J1.pulse
  N3: Parça1.D4, LED1.anode
  VIN: Parça1.VIN, S1.COM, J1.vcc
  3V3: Parça1.3V3, Mod1.Vin
  N4: S1.L2, VCC2.+

custom parts:
  KY-005 Infrared Transmitter Module: Arduino IR Transmitter Module Keyes KY-005, emits infrared light at 38KHz.
